# Fritzing sketch stove-side (saved by Fritzing 0.9.3b)

parts:
  Adafruit_HUZZAH_ESP8266_Breakout1 = Adafruit HUZZAH ESP8266 Breakout [part_number=2471]
  J2 = Camdenboss CTB0158-8 [part_number=CTB0158-8 package=THT]
  M1 = RioRand LM2596
  Part1 = Adafruit MCP9808 [part_number="Adafruit #5027"]
  Actual_the_NON-LATCHING_version = Adafruit Latching Mini Relay FeatherWing [part_number="Adafruit #2923"]

nets:
  GND: Adafruit_HUZZAH_ESP8266_Breakout1.GND, M1.Pin_4, Part1.GND, Actual_the_NON-LATCHING_version.SCK, Actual_the_NON-LATCHING_version.GND
  N1: Adafruit_HUZZAH_ESP8266_Breakout1.V+, M1.Pin_3, Actual_the_NON-LATCHING_version.EN
  N2: Adafruit_HUZZAH_ESP8266_Breakout1.#13, Actual_the_NON-LATCHING_version.USB
  N3: Adafruit_HUZZAH_ESP8266_Breakout1.#12, Actual_the_NON-LATCHING_version.N, Actual_the_NON-LATCHING_version.SET
  N4: Adafruit_HUZZAH_ESP8266_Breakout1.#14, Actual_the_NON-LATCHING_version.M
  N5: Adafruit_HUZZAH_ESP8266_Breakout1.#16, Actual_the_NON-LATCHING_version.L
  N6: Adafruit_HUZZAH_ESP8266_Breakout1.EN, Actual_the_NON-LATCHING_version.K
  N7: Adafruit_HUZZAH_ESP8266_Breakout1.A, Actual_the_NON-LATCHING_version.J
  N8: Adafruit_HUZZAH_ESP8266_Breakout1.RST, Actual_the_NON-LATCHING_version.I
  N9: Adafruit_HUZZAH_ESP8266_Breakout1.#4, Part1.SCL, Actual_the_NON-LATCHING_version.F
  N10: Adafruit_HUZZAH_ESP8266_Breakout1.#0, Part1.SDA, Actual_the_NON-LATCHING_version.E
  N11: Adafruit_HUZZAH_ESP8266_Breakout1.#15, Actual_the_NON-LATCHING_version.C
  N12: Adafruit_HUZZAH_ESP8266_Breakout1.3V, Actual_the_NON-LATCHING_version.B
  VCC: Adafruit_HUZZAH_ESP8266_Breakout1.LDO, Part1.VCC, Actual_the_NON-LATCHING_version.MOSI, Actual_the_NON-LATCHING_version.A, Actual_the_NON-LATCHING_version.3.3V
  N13: J2.pin1, M1.Pin_1, Actual_the_NON-LATCHING_version.COM
  N14: J2.pin4, Actual_the_NON-LATCHING_version.NO
  N15: J2.pin8, M1.Pin_2

notes:
  12vdc

custom parts:
  Adafruit MCP9808: The MCP9808 digital temperature sensor is one of the more accurate/precise we've ever seen, with a typical accuracy of ±0.25°C over the sensor's -40°C to +125°C range and precision of +0.0625°C. They work great with any microcontroller using standard I2C. With three address jumpers on the back, you can connect up to 8 to a single I2C bus without address collisions. Best of all, a wide voltage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
  Adafruit Latching Mini Relay FeatherWing: A Feather board without ambition is a Feather board without FeatherWings! This is the Latching Mini Relay FeatherWing. It gives you power to control, and control over power. Put simply, you can now turn on and off lamps, fans, solenoids, and other small appliances that run on up to 250VAC or DC power using any Feather board. The are two 'flavors' of these FeatherWings, this is the Latching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
